// Digital circuit And4-1.dig as structural Verilog
module And4_1 (
  input  [3:0] in4,
  input  in1,
  output [3:0] out
);

  and and_1 (out[0], in4[0], in1);
  and and_2 (out[1], in4[1], in1);
  and and_3 (out[2], in4[2], in1);
  and and_4 (out[3], in4[3], in1);

  // Notes on the sheet:
  //   AND-4-1
endmodule
