// Digital circuit DFFE4.dig as structural Verilog
module DFFE4 (
  input  ENA,
  input  CLK,
  input  [3:0] D,
  output [3:0] Q
);

  wire driver_1_out;

  assign driver_1_out = ENA ? CLK : 1'bz;  // Driver driver_1
  D_FF #(.Bits(4)) d_ff_1 (.D(D), .C(driver_1_out), .Q(Q));  // open: nQ

  // Notes on the sheet:
  //   DFFE4
endmodule
