// Digital circuit T_AS.dig as structural Verilog
module T_AS (
  input  T,
  input  Clk,
  input  Clr,
  output Q,
  output Q_2
);

  wire not_1_out, xor_1_out;

  xor xor_1 (xor_1_out, Q, T);
  not not_1 (not_1_out, Clr);
  D_FF_AS d_ff_as_1 (.Set(1'b0), .D(xor_1_out), .C(Clk), .Clr(not_1_out), .Q(Q), .nQ(Q_2));

  // Notes on the sheet:
  //   T Flip Flop with asynchronous clear
endmodule
