// Digital circuit alu.dig as structural Verilog
module alu (
  input  [7:0] db,
  input  alu_oe,
  input  alu_shift_right,
  input  alu_shift_left,
  input  alu_shift_in,
  input  alu_shiht_oe,
  input  alu_op2_oe,
  input  clk,
  input  alu_op2_sel_bus,
  input  alu_op2_sel_lq,
  input  alu_op2_sel_zero,
  input  alu_sel_op2_neg,
  input  alu_sel_op2_high,
  input  alu_core_R,
  input  alu_core_V,
  input  alu_core_S,
  input  alu_core_cf_in,
  input  alu_parity_in,
  input  alu_op_low,
  input  alu_res_oe,
  input  alu_op1_oe,
  input  alu_op1_sel_bus,
  input  alu_op1_sel_low,
  input  alu_op1_sel_zero,
  input  alu_bs_oe,
  input  [2:0] bse,
  output alu_sf_out,
  output alu_yf_out,
  output alu_parity_out,
  output alu_core_cf_out,
  output alu_vf_out,
  output alu_zero,
  output [3:0] test_db_low,
  output [3:0] test_db_high,
  output alu_shift_db0,
  output alu_shiht_db7,
  output alu_low_gt_9,
  output alu_high_gt_9,
  output alu_high_eq_9
);

  wire not_1_out, not_4_out, not_5_out, not_6_out, not_7_out, op1_latch_mux_high_ena, op1_latch_mux_low_ena,
       op2_latch_mux_high_ena, op2_latch_mux_low_p2, xor_1_out, xor_2_out, xor_3_out;
  wire [3:0] alu_core_1_result, alu_shifter_core_out_high, alu_shifter_core_out_low, and4_1_1_out,
       and4_1_2_out, and4_1_3_out, and4_1_4_out, and4_1_5_out, and4_1_6_out, and4_1_7_out, and4_1_8_out,
       dffe4_1_q, dffe4_2_q, dffe4_3_q, dffe4_4_q, dffe4_5_q, input_bit_sel_p1, input_bit_sel_p2, not_2_out,
       not_3_out, op1_latch_mux_high_q, op1_latch_mux_low_q, op2_latch_mux_high_q, op2_latch_mux_low_p1,
       op2_latch_mux_low_p5, or_4_4_1_out4, or_4_4_2_out4, or_4_4_3_out4;

  assign db[3:0] = alu_oe ? test_db_low : 4'bz;  // Driver driver_1
  assign db[7:4] = alu_oe ? {alu_sf_out, test_db_high[2], alu_yf_out, test_db_high[0]} : 4'bz;  // Driver driver_2
  alu_shifter_core alu_shifter_core (
    .db(db), .shift_in(alu_shift_in), .shift_right(alu_shift_right), .shift_left(alu_shift_left),
    .shift_db0(alu_shift_db0), .shift_db7(alu_shiht_db7), .out_low(alu_shifter_core_out_low),
    .out_high(alu_shifter_core_out_high));
  assign test_db_low = alu_shiht_oe ? alu_shifter_core_out_low : 4'bz;  // Driver driver_3
  assign {alu_sf_out, test_db_high[2], alu_yf_out, test_db_high[0]} = alu_shiht_oe ? alu_shifter_core_out_high : 4'bz;  // Driver driver_4
  assign test_db_low = alu_op2_oe ? dffe4_1_q : 4'bz;  // Driver driver_5
  assign {alu_sf_out, test_db_high[2], alu_yf_out, test_db_high[0]} = alu_op2_oe ? dffe4_2_q : 4'bz;  // Driver driver_6
  not not_1 (not_1_out, clk);
  DFFE4 dffe4_1 (.ENA(op2_latch_mux_low_p2), .CLK(not_1_out), .D(op2_latch_mux_low_p1), .Q(dffe4_1_q));
  DFFE4 dffe4_2 (.ENA(op2_latch_mux_high_ena), .CLK(not_1_out), .D(op2_latch_mux_high_q), .Q(dffe4_2_q));
  // alu_mux_3z op2_latch_mux_low: pin names not known; wires that end beside it: op2_latch_mux_low_p1, op2_latch_mux_low_p2, test_db_low, alu_op2_sel_bus, op2_latch_mux_low_p5, alu_op2_sel_lq, alu_op2_sel_zero
  alu_mux_3z op2_latch_mux_high (
    .a({alu_sf_out, test_db_high[2], alu_yf_out, test_db_high[0]}), .sel_a(alu_op2_sel_bus), .b(test_db_low),
    .sel_b(alu_op2_sel_lq), .sel_zero(alu_op2_sel_zero), .Q(op2_latch_mux_high_q),
    .ena(op2_latch_mux_high_ena));
  assign not_2_out = ~dffe4_2_q;  // Not not_2, 4 bits wide
  assign not_3_out = ~dffe4_1_q;  // Not not_3, 4 bits wide
  not not_4 (not_4_out, alu_sel_op2_neg);
  And4_1 and4_1_1 (.in4(dffe4_1_q), .in1(alu_sel_op2_neg), .out(and4_1_1_out));
  And4_1 and4_1_2 (.in4(not_3_out), .in1(not_4_out), .out(and4_1_2_out));
  And4_1 and4_1_3 (.in4(dffe4_2_q), .in1(alu_sel_op2_neg), .out(and4_1_3_out));
  And4_1 and4_1_4 (.in4(not_2_out), .in1(not_4_out), .out(and4_1_4_out));
  or_4_4 or_4_4_1 (.ina4(and4_1_1_out), .inb4(and4_1_2_out), .out4(or_4_4_1_out4));
  or_4_4 or_4_4_2 (.ina4(and4_1_3_out), .inb4(and4_1_4_out), .out4(or_4_4_2_out4));
  not not_5 (not_5_out, alu_sel_op2_high);
  And4_1 and4_1_5 (.in4(or_4_4_1_out4), .in1(not_5_out), .out(and4_1_5_out));
  And4_1 and4_1_6 (.in4(or_4_4_2_out4), .in1(alu_sel_op2_high), .out(and4_1_6_out));
  or_4_4 or_4_4_3 (.ina4(and4_1_5_out), .inb4(and4_1_6_out), .out4(or_4_4_3_out4));
  alu_core alu_core_1 (
    .op1(op2_latch_mux_low_p5), .op2(or_4_4_3_out4), .cy_in(alu_core_cf_in), .S(alu_core_S), .V(alu_core_V),
    .R(alu_core_R), .result(alu_core_1_result), .cy_out(alu_core_cf_out), .vf_out(alu_vf_out));
  xor xor_1 (xor_1_out, alu_parity_in, alu_core_1_result[3]);
  xor xor_2 (xor_2_out, xor_1_out, alu_core_1_result[2]);
  xor xor_3 (xor_3_out, xor_2_out, alu_core_1_result[1]);
  xor xor_4 (alu_parity_out, xor_3_out, alu_core_1_result[0]);
  and and_1 (alu_zero, ~test_db_low[0], ~test_db_low[1], ~test_db_low[2], ~test_db_low[3], ~test_db_high[0], ~alu_yf_out, ~test_db_high[2], ~alu_sf_out);  // And
  assign {alu_sf_out, test_db_high[2], alu_yf_out, test_db_high[0]} = alu_res_oe ? alu_core_1_result : 4'bz;  // Driver driver_7
  DFFE4 dffe4_3 (.ENA(alu_op_low), .CLK(clk), .D(alu_core_1_result), .Q(dffe4_3_q));
  assign test_db_low = alu_res_oe ? dffe4_3_q : 4'bz;  // Driver driver_8
  or_4_4 or_4_4_4 (.ina4(and4_1_8_out), .inb4(and4_1_7_out), .out4(op2_latch_mux_low_p5));
  And4_1 and4_1_7 (.in4(dffe4_4_q), .in1(alu_op_low), .out(and4_1_7_out));
  And4_1 and4_1_8 (.in4(dffe4_5_q), .in1(not_6_out), .out(and4_1_8_out));
  not not_6 (not_6_out, alu_op_low);
  assign test_db_low = alu_op1_oe ? dffe4_4_q : 4'bz;  // Driver driver_9
  assign {alu_sf_out, test_db_high[2], alu_yf_out, test_db_high[0]} = alu_op1_oe ? dffe4_5_q : 4'bz;  // Driver driver_10
  DFFE4 dffe4_4 (.ENA(op1_latch_mux_low_ena), .CLK(not_7_out), .D(op1_latch_mux_low_q), .Q(dffe4_4_q));
  alu_prep_daa prep_daa (
    .low(dffe4_4_q), .low_gt_9(alu_low_gt_9), .high(dffe4_5_q), .high_gt_9(alu_high_gt_9),
    .high_eq_9(alu_high_eq_9));
  DFFE4 dffe4_5 (.ENA(op1_latch_mux_high_ena), .CLK(clk), .D(op1_latch_mux_high_q), .Q(dffe4_5_q));
  not not_7 (not_7_out, clk);
  alu_mux_3z op1_latch_mux_low (
    .a(test_db_low), .sel_a(alu_op1_sel_bus), .b({alu_sf_out, test_db_high[2], alu_yf_out, test_db_high[0]}),
    .sel_b(alu_op1_sel_low), .sel_zero(alu_op1_sel_zero), .Q(op1_latch_mux_low_q), .ena(op1_latch_mux_low_ena));
  alu_mux_2z op1_latch_mux_high (
    .a({alu_sf_out, test_db_high[2], alu_yf_out, test_db_high[0]}), .sel_a(alu_op1_sel_bus),
    .sel_zero(alu_op1_sel_zero), .ena(op1_latch_mux_high_ena), .Q(op1_latch_mux_high_q));
  assign test_db_low = alu_bs_oe ? input_bit_sel_p1 : 4'bz;  // Driver driver_11
  assign {alu_sf_out, test_db_high[2], alu_yf_out, test_db_high[0]} = alu_bs_oe ? input_bit_sel_p2 : 4'bz;  // Driver driver_12
  // alu_bit_select input_bit_sel: pin names not known; wires that end beside it: input_bit_sel_p1, input_bit_sel_p2, bse

  assign {test_db_high[3], test_db_high[1]} = {alu_sf_out, alu_yf_out};

  // Notes on the sheet:
  //   db[3..0]
  //   db[7..4]
endmodule
