// Digital circuit alu_4_mux.dig as structural Verilog
module alu_4_mux (
  input  [1:0] sel,
  input  in0,
  input  in1,
  input  in2,
  input  in3,
  output out
);

  wire and_1_out, and_2_out, and_3_out, and_4_out, not_1_out, not_2_out;

  not not_1 (not_1_out, sel[1]);
  not not_2 (not_2_out, sel[0]);
  and and_1 (and_1_out, not_2_out, not_1_out, in0);
  and and_2 (and_2_out, sel[0], not_1_out, in1);
  and and_3 (and_3_out, not_2_out, sel[1], in2);
  and and_4 (and_4_out, sel[0], sel[1], in3);
  or or_1 (out, and_1_out, and_2_out, and_3_out, and_4_out);

  // Notes on the sheet:
  //   alu 4 mux
endmodule
