// Digital circuit alu_8_mux.dig as structural Verilog
module alu_8_mux (
  input  [2:0] sel,
  input  in0,
  input  in1,
  input  in2,
  input  in3,
  input  in4,
  input  in5,
  input  in6,
  input  in7,
  output out
);

  wire and_1_out, and_2_out, and_3_out, and_4_out, and_5_out, and_6_out, and_7_out, and_8_out, not_1_out,
       not_2_out, not_3_out;

  not not_1 (not_1_out, sel[2]);
  not not_2 (not_2_out, sel[1]);
  not not_3 (not_3_out, sel[0]);
  and and_1 (and_1_out, not_3_out, not_2_out, not_1_out, in0);
  and and_2 (and_2_out, sel[0], not_2_out, not_1_out, in1);
  and and_3 (and_3_out, not_3_out, sel[1], not_1_out, in2);
  and and_4 (and_4_out, sel[0], sel[1], not_1_out, in3);
  and and_5 (and_5_out, not_3_out, not_2_out, sel[2], in4);
  and and_6 (and_6_out, sel[0], not_2_out, sel[2], in5);
  and and_7 (and_7_out, not_3_out, sel[1], sel[2], in6);
  and and_8 (and_8_out, sel[0], sel[1], sel[2], in7);
  or or_1 (out, and_1_out, and_2_out, and_3_out, and_4_out, and_5_out, and_6_out, and_7_out, and_8_out);

  // Notes on the sheet:
  //   alu mux 8
endmodule
