// Digital circuit alu_bit_select.dig as structural Verilog
module alu_bit_select (
  input  [2:0] bse,
  output [3:0] bs_out_low,
  output [3:0] bs_out_hi
);

  wire not_1_out, not_2_out, not_3_out;

  not not_1 (not_1_out, bse[0]);
  not not_2 (not_2_out, bse[1]);
  not not_3 (not_3_out, bse[2]);
  and and_1 (bs_out_low[0], not_1_out, not_2_out, not_3_out);
  and and_2 (bs_out_low[1], bse[0], not_2_out, not_3_out);
  and and_3 (bs_out_low[2], not_1_out, bse[1], not_3_out);
  and and_4 (bs_out_low[3], bse[0], bse[1], not_3_out);
  and and_5 (bs_out_hi[0], not_1_out, not_2_out, bse[2]);
  and and_6 (bs_out_hi[1], bse[0], not_2_out, bse[2]);
  and and_7 (bs_out_hi[2], not_1_out, bse[1], bse[2]);
  and and_8 (bs_out_hi[3], bse[0], bse[1], bse[2]);
  // Pins of 1 and 4 bits meet at bs_out_hi

  // Notes on the sheet:
  //   alu bit select
endmodule
