// Digital circuit alu_control.dig as structural Verilog
module alu_control (
  input  alu_shift_db7,
  input  alu_shift_add,
  input  ctl_shift_in,
  input  [2:0] op543,
  input  flags_cf_latch,
  input  ctl_cond_short,
  input  flags_zf,
  input  flags_cf,
  input  flags_pf,
  input  flags_sf,
  input  clk,
  input  ctl_eval_cond,
  input  ctl_daa_oe,
  input  ctl_66_oe,
  input  alu_low_gt_9,
  input  flags_hf2,
  input  alu_high_eq_9,
  input  alu_high_gt_9,
  input  alu_parity_out,
  input  ctl_alu_low,
  input  [1:0] ctl_pf_sel,
  input  alu_vf_out,
  input  iff2,
  input  repeat_en,
  input  ctl_alu_core_hf,
  input  flags_hf,
  output shift_cf_out,
  output alu_shift_in,
  output alu_shift_right,
  output alu_shift_left,
  output flags_cond_true,
  output [7:0] db,
  output daa_cf_out,
  output alu_parity_in,
  output alu_op_low,
  output pf_sel,
  output alu_core_cf_in
);

  wire and_2_out, and_3_out, and_4_out, and_7_out, and_8_out, dffe_1_p4, inst_cond_mux_out, not_1_out,
       not_2_out, not_3_out, not_4_out, not_6_out, or_1_out, or_2_out, or_4_out, xor_1_out;
  wire [1:0] not_5_out;
  wire [6:1] not_7_out;

  not not_1 (not_1_out, ctl_cond_short);
  not not_2 (not_2_out, op543[0]);
  not not_3 (not_3_out, op543[0]);
  not not_4 (not_4_out, op543[0]);
  not not_5 (not_5_out[0], op543[1]);
  and and_1 (not_5_out[1], op543[2], not_1_out);
  or or_1 (or_1_out, ctl_daa_oe, ctl_66_oe);
  or or_2 (or_2_out, alu_low_gt_9, flags_hf2);
  and and_2 (and_2_out, alu_low_gt_9, alu_high_eq_9);
  // dffe dffe_1: pin names not known; wires that end beside it: alu_parity_out, clk, ctl_alu_low, dffe_1_p4
  and and_3 (and_3_out, alu_shift_db7, not_2_out);
  and and_4 (and_4_out, alu_shift_add, op543[0]);
  and and_5 (alu_shift_left, ctl_shift_in, not_3_out);
  and and_6 (alu_shift_right, ctl_shift_in, op543[0]);
  alu_8_mux inst_shift_mux (
    .sel(op543), .in0(alu_shift_db7), .in1(alu_shift_add), .in2(flags_cf_latch), .in3(flags_cf_latch),
    .in4(1'b0), .in5(alu_shift_db7), .in6(1'b1), .in7(1'b0), .out(alu_shift_in));
  or or_3 (alu_parity_in, dffe_1_p4, ctl_alu_low);
  alu_4_mux inst_pf_sel (
    .sel(ctl_pf_sel), .in0(alu_parity_out), .in1(alu_vf_out), .in2(iff2), .in3(repeat_en), .out(pf_sel));
  and and_7 (and_7_out, ctl_alu_core_hf, flags_hf);
  and and_8 (and_8_out, not_6_out, flags_cf_latch);
  not not_6 (not_6_out, ctl_alu_core_hf);
  or or_4 (or_4_out, ctl_66_oe, or_2_out);
  or or_5 (daa_cf_out, ctl_66_oe, and_2_out, alu_high_gt_9, flags_cf_latch);
  or or_6 (shift_cf_out, and_3_out, and_4_out);
  or or_7 (alu_core_cf_in, and_7_out, and_8_out);
  alu_4_mux inst_cond_mux (
    .sel(not_5_out), .in0(flags_zf), .in1(flags_cf), .in2(flags_pf), .in3(flags_sf), .out(inst_cond_mux_out));
  not not_7 (not_7_out[1], or_4_out);
  not not_8 (not_7_out[2], or_4_out);
  not not_9 (not_7_out[5], daa_cf_out);
  not not_10 (not_7_out[6], daa_cf_out);
  xor xor_1 (xor_1_out, not_4_out, inst_cond_mux_out);
  // dffe dffe_2: pin names not known; wires that end beside it: xor_1_out, clk, ctl_eval_cond, flags_cond_true
  assign db = or_1_out ? {1'b0, not_7_out[6:5], 2'b00, not_7_out[2:1], 1'b0} : 8'bz;  // Driver driver_1

  assign alu_op_low = ctl_alu_low;

  // Notes on the sheet:
  //   Select cf out based on the shift direction
  //   op543[0]
  //   op543[1]
  //   op543[2]
  //   Half-parity-control
  //   DAA + bus(66) logic
  //   sel[0]
  //   sel[1]
  //   Parity/Overflow input selector
  //   Carry flag into ALU core
  //   Bit that is shifted in depends on the opcode:
  //   000 RLC -> old D[7]
  //   001 RRC -> old D[0]
  //   010 RL -> CF
  //   011 RR ->CF
  //   100 SLA -> 0
  //   101 SRA -> D[7]
  //   110 SLL -> 1
  //   111 SRL -> 0
  //   Low nibble 0x6
  //   High nibble 0x6
  //   sel[1..0]
  //   Flag condition mux
  //   out[0]
  //   out[1]
  //   out[2]
  //   out[3]
  //   out[4]
  //   out[6]
  //   out[7]
  //   out[7..0]
endmodule
