// Digital circuit alu_core.dig as structural Verilog
module alu_core (
  input  [3:0] op1,
  input  [3:0] op2,
  input  cy_in,
  input  S,
  input  V,
  input  R,
  output [3:0] result,
  output cy_out,
  output vf_out
);

  wire alu_slice_1_cy_out, alu_slice_2_cy_out, alu_slice_3_cy_out;

  alu_slice alu_slice_1 (
    .op1(op1[0]), .op2(op2[0]), .S(S), .R(R), .cy_in(cy_in), .cy_out(alu_slice_1_cy_out), .result(result[0]),
    .V(V));
  alu_slice alu_slice_2 (
    .op1(op1[1]), .op2(op2[1]), .S(S), .R(R), .cy_in(alu_slice_1_cy_out), .cy_out(alu_slice_2_cy_out),
    .result(result[1]), .V(V));
  alu_slice alu_slice_3 (
    .op1(op1[2]), .op2(op2[2]), .S(S), .R(R), .cy_in(alu_slice_2_cy_out), .cy_out(alu_slice_3_cy_out),
    .result(result[2]), .V(V));
  alu_slice alu_slice_4 (
    .op1(op1[3]), .op2(op2[3]), .S(S), .R(R), .cy_in(alu_slice_3_cy_out), .cy_out(cy_out),
    .result(result[3]), .V(V));
  xor xor_1 (vf_out, cy_out, alu_slice_3_cy_out);
endmodule
