// Digital circuit alu_flags.dig as structural Verilog
module alu_flags (
  input  ctl_flags_oe,
  input  ctl_flags_bus,
  input  ctl_flags_alu,
  input  alu_sf_out,
  input  ctl_flags_sz_we,
  input  alu_zero,
  input  ctl_alu_zero_16bit,
  input  alu_yf_out,
  input  ctl_flags_xy_we,
  input  ctl_flags_hf_we,
  input  ctl_flags_hf_cpl,
  input  ctl_flags_hf2_we,
  input  alu_xf_out,
  input  pf_sel,
  input  ctl_flags_nf_set,
  input  ctl_flags_pf_we,
  input  ctl_flags_nf_clr,
  input  ctl_flags_nf_we,
  input  alu_core_cf_out,
  input  ctl_flags_cf_we,
  input  ctl_flags_cf2_we,
  input  ctl_flags_cf2_shift,
  input  ctl_flags_cf2_daa,
  input  shift_cf_out,
  input  daa_cf_out,
  input  clk,
  input  ctl_flags_use_cf2,
  input  ctl_flags_cf_set,
  input  ctl_flags_set_cpl,
  output [7:0] db,
  output flags_sf,
  output flags_zf,
  output flags_hf,
  output flags_hf2,
  output flags_cf_latch,
  output flags_cf
);

  wire alu_4_mux_1_out, alu_mux_2_1_out, and_1_out, and_2_out, and_3_out, and_4_out, and_5_out, and_6_out,
       and_7_out, and_8_out, and_9_out, and_10_out, and_11_out, and_12_out, and_13_out, and_14_out,
       and_15_out, and_16_out, and_17_out, and_18_out, and_19_out, dffe_2_p5, dffe_5_p4, dffe_6_p4,
       dffe_8_p4, dffe_9_p4, dffe_10_p4, not_1_out, not_2_out, not_3_out, or_1_out, or_2_out, or_3_out,
       or_4_out, or_5_out, or_6_out, or_7_out, or_8_out, or_9_out, or_10_out;

  and and_1 (and_1_out, db[7], ctl_flags_bus);
  and and_2 (and_2_out, alu_sf_out, ctl_flags_alu);
  and and_3 (and_3_out, db[6], ctl_flags_bus);
  and and_4 (and_4_out, alu_zero, ctl_flags_alu);
  and and_5 (and_5_out, db[5], ctl_flags_bus);
  and and_6 (and_6_out, alu_yf_out, ctl_flags_alu);
  and and_7 (and_7_out, db[4], ctl_flags_bus);
  and and_8 (and_8_out, alu_core_cf_out, ctl_flags_alu);
  and and_9 (and_9_out, db[3], ctl_flags_bus);
  and and_10 (and_10_out, alu_xf_out, ctl_flags_alu);
  and and_11 (and_11_out, db[2], ctl_flags_bus);
  and and_12 (and_12_out, pf_sel, ctl_flags_alu);
  and and_13 (and_13_out, db[1], ctl_flags_bus);
  and and_14 (and_14_out, alu_sf_out, ctl_flags_alu);
  and and_15 (and_15_out, db[0], ctl_flags_bus);
  and and_16 (and_16_out, ctl_flags_alu, alu_core_cf_out);
  not not_1 (not_1_out, ctl_flags_cf2_we);
  alu_4_mux alu_4_mux_1 (
    .sel({ctl_flags_cf2_daa, ctl_flags_cf2_shift}), .in0(alu_core_cf_out), .in1(shift_cf_out),
    .in2(daa_cf_out), .in3(1'b0), .out(alu_4_mux_1_out));
  not not_2 (not_2_out, ctl_alu_zero_16bit);
  or or_1 (or_1_out, and_1_out, and_2_out);
  or or_2 (or_2_out, and_3_out, and_4_out);
  or or_3 (or_3_out, flags_zf, not_2_out);
  or or_4 (or_4_out, and_5_out, and_6_out);
  or or_5 (or_5_out, and_7_out, and_8_out);
  or or_6 (or_6_out, and_9_out, and_10_out);
  or or_7 (or_7_out, and_11_out, and_12_out);
  or or_8 (or_8_out, and_13_out, ctl_flags_nf_set, and_14_out);
  not not_3 (not_3_out, ctl_flags_nf_clr);
  or or_9 (or_9_out, and_15_out, and_16_out);
  and and_17 (and_17_out, ctl_flags_cf_we, not_1_out);
  and and_18 (and_18_out, or_2_out, or_3_out);
  and and_19 (and_19_out, or_8_out, not_3_out);
  // dffe dffe_1: pin names not known; wires that end beside it: or_9_out, clk, and_17_out, flags_cf_latch
  // dffe dffe_2: pin names not known; wires that end beside it: alu_4_mux_1_out, alu_4_mux_1_out, clk, ctl_flags_cf2_we, dffe_2_p5
  // dffe dffe_3: pin names not known; wires that end beside it: or_1_out, clk, ctl_flags_sz_we, flags_sf
  // dffe dffe_4: pin names not known; wires that end beside it: and_18_out, clk, ctl_flags_sz_we, flags_zf
  // dffe dffe_5: pin names not known; wires that end beside it: or_4_out, clk, ctl_flags_xy_we, dffe_5_p4
  // dffe dffe_6: pin names not known; wires that end beside it: or_5_out, clk, ctl_flags_hf_we, dffe_6_p4
  // dffe dffe_7: pin names not known; wires that end beside it: or_5_out, clk, ctl_flags_hf2_we, flags_hf2
  // dffe dffe_8: pin names not known; wires that end beside it: or_6_out, clk, ctl_flags_xy_we, dffe_8_p4
  // dffe dffe_9: pin names not known; wires that end beside it: or_7_out, clk, ctl_flags_pf_we, dffe_9_p4
  // dffe dffe_10: pin names not known; wires that end beside it: and_19_out, clk, ctl_flags_nf_we, dffe_10_p4
  alu_mux_2 alu_mux_2_1 (.in0(flags_cf_latch), .in1(dffe_2_p5), .sel1(ctl_flags_use_cf2), .out(alu_mux_2_1_out));
  assign db[7] = ctl_flags_oe ? flags_sf : 1'bz;  // Driver driver_1
  assign db[6] = ctl_flags_oe ? flags_zf : 1'bz;  // Driver driver_2
  assign db[5] = ctl_flags_oe ? dffe_5_p4 : 1'bz;  // Driver driver_3
  assign db[4] = ctl_flags_oe ? dffe_6_p4 : 1'bz;  // Driver driver_4
  xor xor_1 (flags_hf, dffe_6_p4, ctl_flags_hf_cpl);
  assign db[3] = ctl_flags_oe ? dffe_8_p4 : 1'bz;  // Driver driver_5
  assign db[2] = ctl_flags_oe ? dffe_9_p4 : 1'bz;  // Driver driver_6
  assign db[1] = ctl_flags_oe ? dffe_10_p4 : 1'bz;  // Driver driver_7
  assign db[0] = ctl_flags_oe ? flags_cf : 1'bz;  // Driver driver_8
  or or_10 (or_10_out, alu_mux_2_1_out, ctl_flags_cf_set);
  xor xor_2 (flags_cf, or_10_out, ctl_flags_set_cpl);

  // Notes on the sheet:
  //   alu flags
  //   Sign Flag
  //   Zero Flag
  //   Y Flag
  //   H Flag
  //   X Flag
  //   Parity Flag
  //   N Flag
  //   Carry Flag
  //   Primary Latch
  //   Secondary Latch
  //   Force Set
  //   Force Complement
endmodule
