// Digital circuit alu_mux_2.dig as structural Verilog
module alu_mux_2 (
  input  in0,
  input  in1,
  input  sel1,
  output out
);

  wire and_1_out, and_2_out, not_1_out;

  not not_1 (not_1_out, sel1);
  and and_1 (and_1_out, in0, not_1_out);
  and and_2 (and_2_out, in1, sel1);
  or or_1 (out, and_1_out, and_2_out);

  // Notes on the sheet:
  //   alu mux 2
endmodule
