// Digital circuit alu_mux_2z.dig as structural Verilog
module alu_mux_2z (
  input  [3:0] a,
  input  sel_a,
  input  sel_zero,
  output [3:0] Q,
  output ena
);

  wire and_1_out, and_2_out, and_3_out, and_4_out, not_1_out;

  and and_1 (and_1_out, a[0], sel_a);
  and and_2 (and_2_out, a[1], sel_a);
  and and_3 (and_3_out, a[2], sel_a);
  and and_4 (and_4_out, a[3], sel_a);
  not not_1 (not_1_out, sel_zero);
  and and_5 (Q[0], and_1_out, not_1_out);
  and and_6 (Q[1], and_2_out, not_1_out);
  and and_7 (Q[2], and_3_out, not_1_out);
  and and_8 (Q[3], and_4_out, not_1_out);
  or or_1 (ena, sel_a, sel_zero);

  // Notes on the sheet:
  //   alu mux 2z
endmodule
