// Digital circuit alu_mux_3z.dig as structural Verilog
module alu_mux_3z (
  input  [3:0] a,
  input  sel_a,
  input  [3:0] b,
  input  sel_b,
  input  sel_zero,
  output [3:0] Q,
  output ena
);

  wire and_1_out, and_2_out, and_3_out, and_4_out, and_5_out, and_6_out, and_7_out, and_8_out, not_1_out,
       or_2_out, or_3_out, or_4_out, or_5_out;

  and and_1 (and_1_out, a[0], sel_a);
  and and_2 (and_2_out, a[1], sel_a);
  and and_3 (and_3_out, a[2], sel_a);
  and and_4 (and_4_out, a[3], sel_a);
  and and_5 (and_5_out, b[0], sel_b);
  and and_6 (and_6_out, b[1], sel_b);
  and and_7 (and_7_out, b[2], sel_b);
  and and_8 (and_8_out, b[3], sel_b);
  or or_1 (ena, sel_zero, sel_b, sel_a);
  or or_2 (or_2_out, and_1_out, and_5_out);
  or or_3 (or_3_out, and_2_out, and_6_out);
  or or_4 (or_4_out, and_3_out, and_7_out);
  or or_5 (or_5_out, and_4_out, and_8_out);
  not not_1 (not_1_out, sel_zero);
  and and_9 (Q[0], or_2_out, not_1_out);
  and and_10 (Q[1], or_3_out, not_1_out);
  and and_11 (Q[2], or_4_out, not_1_out);
  and and_12 (Q[3], or_5_out, not_1_out);

  // Notes on the sheet:
  //   alu mux 3z
endmodule
