// Digital circuit alu_prep_daa.dig as structural Verilog
module alu_prep_daa (
  input  [3:0] low,
  input  [3:0] high,
  output low_gt_9,
  output high_gt_9,
  output high_eq_9
);

  wire and_1_out, and_2_out, and_3_out, and_4_out, not_1_out, not_2_out;

  and and_1 (and_1_out, low[3], low[2]);
  and and_2 (and_2_out, low[3], low[1]);
  and and_3 (and_3_out, high[3], high[2]);
  and and_4 (and_4_out, high[3], high[1]);
  not not_1 (not_1_out, high[2]);
  not not_2 (not_2_out, high[1]);
  or or_1 (low_gt_9, and_1_out, and_2_out);
  or or_2 (high_gt_9, and_3_out, and_4_out);
  and and_5 (high_eq_9, high[3], high[0], not_1_out, not_2_out);

  // Notes on the sheet:
  //   alu prep daa
endmodule
