// Digital circuit alu_shifter_core.dig as structural Verilog
module alu_shifter_core (
  input  [7:0] db,
  input  shift_in,
  input  shift_right,
  input  shift_left,
  output shift_db0,
  output shift_db7,
  output [3:0] out_low,
  output [3:0] out_high
);

  wire and_1_out, and_2_out, and_3_out, and_4_out, and_5_out, and_6_out, and_7_out, and_8_out, and_9_out,
       and_10_out, and_11_out, and_12_out, and_13_out, and_14_out, and_15_out, and_16_out, and_17_out,
       and_18_out, and_19_out, and_20_out, and_21_out, and_22_out, and_23_out, and_24_out, nor_1_out;

  nor nor_1 (nor_1_out, shift_right, shift_left);
  and and_1 (and_1_out, db[6], shift_left);
  and and_2 (and_2_out, db[7], nor_1_out);
  or or_1 (out_high[3], and_3_out, and_2_out, and_1_out);
  and and_3 (and_3_out, shift_in, shift_right);
  and and_4 (and_4_out, db[5], shift_left);
  and and_5 (and_5_out, db[6], nor_1_out);
  or or_2 (out_high[2], and_6_out, and_5_out, and_4_out);
  and and_6 (and_6_out, db[7], shift_right);
  and and_7 (and_7_out, db[4], shift_left);
  and and_8 (and_8_out, db[5], nor_1_out);
  or or_3 (out_high[1], and_9_out, and_8_out, and_7_out);
  and and_9 (and_9_out, db[6], shift_right);
  and and_10 (and_10_out, db[3], shift_left);
  and and_11 (and_11_out, db[4], nor_1_out);
  or or_4 (out_high[0], and_12_out, and_11_out, and_10_out);
  and and_12 (and_12_out, db[5], shift_right);
  and and_13 (and_13_out, db[2], shift_left);
  and and_14 (and_14_out, db[3], nor_1_out);
  or or_5 (out_low[3], and_15_out, and_14_out, and_13_out);
  and and_15 (and_15_out, db[4], shift_right);
  and and_16 (and_16_out, db[1], shift_left);
  and and_17 (and_17_out, db[2], nor_1_out);
  or or_6 (out_low[2], and_18_out, and_17_out, and_16_out);
  and and_18 (and_18_out, db[3], shift_right);
  and and_19 (and_19_out, db[0], shift_left);
  and and_20 (and_20_out, db[1], nor_1_out);
  or or_7 (out_low[1], and_21_out, and_20_out, and_19_out);
  and and_21 (and_21_out, db[2], shift_right);
  and and_22 (and_22_out, shift_in, shift_left);
  and and_23 (and_23_out, db[0], nor_1_out);
  or or_8 (out_low[0], and_24_out, and_23_out, and_22_out);
  and and_24 (and_24_out, db[1], shift_right);

  assign shift_db0 = db[0];
  assign shift_db7 = db[7];

  // Notes on the sheet:
  //   Right
  //   Load
  //   Left
  //   Hi bit 3
  //   Hi bit 2
  //   Hi bit 1
  //   alu-shifter-core
  //   Hi bit 0
  //   Lo bit 3
  //   Lo bit 2
  //   Lo bit 1
  //   Lo bit 0
endmodule
