// Digital circuit alu_slice.dig as structural Verilog
module alu_slice (
  input  op1,
  input  op2,
  input  S,
  input  R,
  input  cy_in,
  input  V,
  output cy_out,
  output result
);

  wire and_1_out, and_2_out, and_3_out, and_4_out, nor_1_out, or_1_out, or_2_out, or_3_out;

  or or_1 (or_1_out, op1, op2);
  and and_1 (and_1_out, cy_in, or_1_out);
  and and_2 (and_2_out, op1, op2);
  nor nor_1 (nor_1_out, and_1_out, and_2_out, S);
  nor nor_2 (cy_out, nor_1_out, R);
  or or_2 (or_2_out, cy_in, op2, op1);
  or or_3 (or_3_out, V, nor_1_out);
  and and_3 (and_3_out, cy_in, op2, op1);
  and and_4 (and_4_out, or_2_out, or_3_out);
  or or_4 (result, and_3_out, and_4_out);

  // Notes on the sheet:
  //   OR1
  //   Carry Computation
  //   AND2
  //   AND1
  //   alu slice
  //   NOR1
  //   NOR2
  //   Internal 
  //   Carry
  //   Result Computation
  //   OR2
  //   OR3
  //   AND3
  //   AND4
  //   OR4
endmodule
