// Digital circuit dffe.dig as structural Verilog
module dffe (
  input  ENA,
  input  CLK,
  input  D,
  output Q
);

  wire driver_1_out;

  assign driver_1_out = ENA ? CLK : 1'bz;  // Driver driver_1
  D_FF d_ff_1 (.D(D), .C(driver_1_out), .Q(Q));  // open: nQ

  // Notes on the sheet:
  //   DFFE
endmodule
