// Digital circuit or-4-4.dig as structural Verilog
module or_4_4 (
  input  [3:0] ina4,
  input  [3:0] inb4,
  output [3:0] out4
);

  or or_1 (out4[0], ina4[0], inb4[0]);
  or or_2 (out4[1], ina4[1], inb4[1]);
  or or_3 (out4[2], ina4[2], inb4[2]);
  or or_4 (out4[3], ina4[3], inb4[3]);

  // Notes on the sheet:
  //   OR-4-4
endmodule
