// Digital circuit reg-file.dig as structural Verilog
module reg_file (
  input  [7:0] db_lo_as_in,
  input  [7:0] db_hi_as_in,
  input  reg_sys_we_lo,
  input  reg_sel_sys_lo,
  input  reg_sel_ir,
  input  reg_sys_we_hi,
  input  reg_sel_sys_hi,
  input  clk,
  input  reg_sel_pc,
  input  reg_sw_4d_hi,
  input  reg_sw_4d_lo,
  input  ctl_sw_4u,
  input  reg_sel_wz,
  input  reg_sel_isp,
  input  reg_sel_iy,
  input  reg_sel_ix,
  input  reg_sel_hl2,
  input  reg_sel_hl,
  input  reg_sel_de2,
  input  reg_sel_de,
  input  reg_sel_bc2,
  input  reg_sel_bc,
  input  reg_sel_af2,
  input  reg_sel_af,
  input  ctl_reg_in_hi,
  input  ctl_reg_in_lo,
  input  ctl_reg_out_hi,
  input  ctl_reg_out_lo,
  input  reg_gp_we,
  input  reg_sel_gp_lo,
  input  [7:0] db_lo_ds_in,
  input  [7:0] db_hi_ds_in,
  input  reg_sel_gp_hi,
  output [7:0] db_lo_as_out,
  output [7:0] db_hi_out,
  output [7:0] db_lo_ds_out,
  output [7:0] db_hi_ds_out
);

  wire AF2_hi_p1, AF2_hi_p4, AF_hi_p1, AF_hi_p4, and_1_out, and_3_out, and_5_out, and_7_out, and_9_out,
       and_11_out, and_13_out, and_15_out, and_17_out, and_19_out, and_21_out, and_23_out, and_25_out,
       and_27_out, and_29_out, and_31_out, and_33_out, and_35_out, and_37_out, and_39_out, and_41_out,
       and_43_out, and_45_out, and_47_out, and_49_out, and_51_out, and_53_out, and_55_out, BC2_hi_p1,
       BC2_hi_p4, BC_hi_p1, BC_hi_p4, DE2_hi_p1, DE2_hi_p4, DE_hi_p1, DE_hi_p4, HL2_hi_p1, HL2_hi_p4,
       HL_hi_p1, HL_hi_p4, IR_hi_p1, IR_hi_p4, IX_hi_p1, IX_hi_p4, IY_hi_p1, IY_hi_p4, not_1_out, not_2_out,
       not_3_out, PC_hi_p1, PC_hi_p4, SP_hi_p1, SP_hi_p4, WZ_hi_p1, WZ_hi_p4;
  wire [7:0] driver_1_out, driver_4_out, driver_5_out, driver_7_out;

  not not_1 (not_1_out, reg_sys_we_lo);
  assign driver_1_out = reg_sys_we_lo ? db_lo_as_in : 8'bz;  // Driver driver_1
  assign db_lo_as_out = not_1_out ? driver_1_out : 8'bz;  // Driver driver_2
  assign db_hi_out = not_2_out ? driver_4_out : 8'bz;  // Driver driver_3
  assign driver_4_out = reg_sys_we_hi ? db_hi_as_in : 8'bz;  // Driver driver_4
  not not_2 (not_2_out, reg_sys_we_hi);
  and and_1 (and_1_out, not_1_out, reg_sel_sys_lo, reg_sel_ir);
  // reg_latch IR_hi: pin names not known; wires that end beside it: IR_hi_p1, driver_4_out, clk, IR_hi_p4
  and and_2 (IR_hi_p1, reg_sel_ir, reg_sys_we_hi, reg_sel_sys_hi);
  and and_3 (and_3_out, reg_sys_we_lo, reg_sel_sys_lo, reg_sel_ir);
  // reg_latch IR_lo: pin names not known; wires that end beside it: and_1_out, clk, driver_1_out, and_3_out
  and and_4 (IR_hi_p4, reg_sel_ir, not_2_out, reg_sel_sys_hi);
  and and_5 (and_5_out, not_1_out, reg_sel_sys_lo, reg_sel_pc);
  // reg_latch PC_hi: pin names not known; wires that end beside it: PC_hi_p1, driver_4_out, clk, PC_hi_p4
  and and_6 (PC_hi_p1, reg_sel_pc, reg_sys_we_hi, reg_sel_sys_hi);
  and and_7 (and_7_out, reg_sys_we_lo, reg_sel_sys_lo, reg_sel_pc);
  // reg_latch PC_lo: pin names not known; wires that end beside it: and_5_out, clk, driver_1_out, and_7_out, ctl_sw_4u
  and and_8 (PC_hi_p4, reg_sel_pc, not_2_out, reg_sel_sys_hi);
  assign driver_5_out = ctl_sw_4u ? driver_1_out : 8'bz;  // Driver driver_5
  assign driver_1_out = reg_sw_4d_lo ? driver_5_out : 8'bz;  // Driver driver_6
  assign driver_7_out = ctl_sw_4u ? driver_4_out : 8'bz;  // Driver driver_7
  assign driver_4_out = reg_sw_4d_hi ? driver_7_out : 8'bz;  // Driver driver_8
  and and_9 (and_9_out, not_1_out, reg_sel_sys_lo, reg_sel_wz);
  // reg_latch WZ_hi: pin names not known; wires that end beside it: WZ_hi_p1, driver_7_out, clk, WZ_hi_p4
  and and_10 (WZ_hi_p1, reg_sel_wz, reg_sys_we_hi, reg_sel_sys_hi);
  and and_11 (and_11_out, reg_sys_we_lo, reg_sel_sys_lo, reg_sel_wz);
  // reg_latch WZ_lo: pin names not known; wires that end beside it: and_9_out, clk, driver_5_out, and_11_out
  and and_12 (WZ_hi_p4, reg_sel_wz, not_2_out, reg_sel_sys_hi);
  and and_13 (and_13_out, not_3_out, reg_sel_gp_lo, reg_sel_isp);
  // reg_latch SP_hi: pin names not known; wires that end beside it: SP_hi_p1, driver_7_out, clk, SP_hi_p4
  and and_14 (SP_hi_p1, reg_sel_isp, not_3_out, reg_sel_gp_hi);
  and and_15 (and_15_out, reg_gp_we, reg_sel_gp_lo, reg_sel_isp);
  // reg_latch SP_lo: pin names not known; wires that end beside it: and_13_out, clk, driver_5_out, and_15_out
  and and_16 (SP_hi_p4, reg_sel_isp, reg_gp_we, reg_sel_gp_hi);
  and and_17 (and_17_out, not_3_out, reg_sel_gp_lo, reg_sel_iy);
  // reg_latch IY_hi: pin names not known; wires that end beside it: IY_hi_p1, driver_7_out, clk, IY_hi_p4
  and and_18 (IY_hi_p1, reg_sel_iy, not_3_out, reg_sel_gp_hi);
  and and_19 (and_19_out, reg_gp_we, reg_sel_gp_lo, reg_sel_iy);
  // reg_latch IY_lo: pin names not known; wires that end beside it: and_17_out, clk, driver_5_out, and_19_out
  and and_20 (IY_hi_p4, reg_sel_iy, reg_gp_we, reg_sel_gp_hi);
  and and_21 (and_21_out, not_3_out, reg_sel_gp_lo, reg_sel_ix);
  // reg_latch IX_hi: pin names not known; wires that end beside it: IX_hi_p1, driver_7_out, clk, IX_hi_p4
  and and_22 (IX_hi_p1, reg_sel_ix, not_3_out, reg_sel_gp_hi);
  and and_23 (and_23_out, reg_gp_we, reg_sel_gp_lo, reg_sel_ix);
  // reg_latch IX_lo: pin names not known; wires that end beside it: and_21_out, clk, driver_5_out, and_23_out
  and and_24 (IX_hi_p4, reg_sel_ix, reg_gp_we, reg_sel_gp_hi);
  and and_25 (and_25_out, not_3_out, reg_sel_gp_lo, reg_sel_hl2);
  // reg_latch HL2_hi: pin names not known; wires that end beside it: HL2_hi_p1, driver_7_out, clk, HL2_hi_p4
  and and_26 (HL2_hi_p1, reg_sel_hl2, not_3_out, reg_sel_gp_hi);
  and and_27 (and_27_out, reg_gp_we, reg_sel_gp_lo, reg_sel_hl2);
  // reg_latch HL2_lo: pin names not known; wires that end beside it: and_25_out, clk, driver_5_out, and_27_out
  and and_28 (HL2_hi_p4, reg_sel_hl2, reg_gp_we, reg_sel_gp_hi);
  and and_29 (and_29_out, not_3_out, reg_sel_gp_lo, reg_sel_hl);
  // reg_latch HL_hi: pin names not known; wires that end beside it: HL_hi_p1, driver_7_out, clk, HL_hi_p4
  and and_30 (HL_hi_p1, reg_sel_hl, not_3_out, reg_sel_gp_hi);
  and and_31 (and_31_out, reg_gp_we, reg_sel_gp_lo, reg_sel_hl);
  // reg_latch HL_lo: pin names not known; wires that end beside it: and_29_out, clk, driver_5_out, and_31_out
  and and_32 (HL_hi_p4, reg_sel_hl, reg_gp_we, reg_sel_gp_hi);
  and and_33 (and_33_out, not_3_out, reg_sel_gp_lo, reg_sel_de2);
  // reg_latch DE2_hi: pin names not known; wires that end beside it: DE2_hi_p1, driver_7_out, clk, DE2_hi_p4
  and and_34 (DE2_hi_p1, reg_sel_de2, not_3_out, reg_sel_gp_hi);
  and and_35 (and_35_out, reg_gp_we, reg_sel_gp_lo, reg_sel_de2);
  // reg_latch DE2_lo: pin names not known; wires that end beside it: and_33_out, clk, driver_5_out, and_35_out
  and and_36 (DE2_hi_p4, reg_sel_de2, reg_gp_we, reg_sel_gp_hi);
  and and_37 (and_37_out, not_3_out, reg_sel_gp_lo, reg_sel_de);
  // reg_latch DE_hi: pin names not known; wires that end beside it: DE_hi_p1, driver_7_out, clk, DE_hi_p4
  and and_38 (DE_hi_p1, reg_sel_de, not_3_out, reg_sel_gp_hi);
  and and_39 (and_39_out, reg_gp_we, reg_sel_gp_lo, reg_sel_de);
  // reg_latch DE_lo: pin names not known; wires that end beside it: and_37_out, clk, driver_5_out, and_39_out
  and and_40 (DE_hi_p4, reg_sel_de, reg_gp_we, reg_sel_gp_hi);
  and and_41 (and_41_out, not_3_out, reg_sel_gp_lo, reg_sel_bc2);
  // reg_latch BC2_hi: pin names not known; wires that end beside it: BC2_hi_p1, driver_7_out, clk, BC2_hi_p4
  and and_42 (BC2_hi_p1, reg_sel_bc2, not_3_out, reg_sel_gp_hi);
  and and_43 (and_43_out, reg_gp_we, reg_sel_gp_lo, reg_sel_bc2);
  // reg_latch BC2_lo: pin names not known; wires that end beside it: and_41_out, clk, driver_5_out, and_43_out
  and and_44 (BC2_hi_p4, reg_sel_bc2, reg_gp_we, reg_sel_gp_hi);
  and and_45 (and_45_out, not_3_out, reg_sel_gp_lo, reg_sel_bc);
  // reg_latch BC_hi: pin names not known; wires that end beside it: BC_hi_p1, driver_7_out, clk, BC_hi_p4
  and and_46 (BC_hi_p1, reg_sel_bc, not_3_out, reg_sel_gp_hi);
  and and_47 (and_47_out, reg_gp_we, reg_sel_gp_lo, reg_sel_bc);
  // reg_latch BC_lo: pin names not known; wires that end beside it: and_45_out, clk, driver_5_out, and_47_out
  and and_48 (BC_hi_p4, reg_sel_bc, reg_gp_we, reg_sel_gp_hi);
  and and_49 (and_49_out, not_3_out, reg_sel_gp_lo, reg_sel_af2);
  // reg_latch AF2_hi: pin names not known; wires that end beside it: AF2_hi_p1, driver_7_out, clk, AF2_hi_p4
  and and_50 (AF2_hi_p1, reg_sel_af2, not_3_out, reg_sel_gp_hi);
  and and_51 (and_51_out, reg_gp_we, reg_sel_gp_lo, reg_sel_af2);
  // reg_latch AF2_lo: pin names not known; wires that end beside it: and_49_out, clk, driver_5_out, and_51_out
  and and_52 (AF2_hi_p4, reg_sel_af2, reg_gp_we, reg_sel_gp_hi);
  and and_53 (and_53_out, not_3_out, reg_sel_gp_lo, reg_sel_af);
  // reg_latch AF_hi: pin names not known; wires that end beside it: AF_hi_p1, driver_7_out, clk, AF_hi_p4
  and and_54 (AF_hi_p1, reg_sel_af, not_3_out, reg_sel_gp_hi);
  and and_55 (and_55_out, reg_gp_we, reg_sel_gp_lo, reg_sel_af);
  // reg_latch AF_lo: pin names not known; wires that end beside it: and_53_out, clk, driver_5_out, and_55_out
  and and_56 (AF_hi_p4, reg_sel_af, reg_gp_we, reg_sel_gp_hi);
  assign db_lo_ds_out = ctl_reg_out_hi ? driver_5_out : 8'bz;  // Driver driver_9
  assign driver_5_out = ctl_reg_in_lo ? db_lo_ds_in : 8'bz;  // Driver driver_10
  assign db_hi_ds_out = ctl_reg_out_lo ? driver_7_out : 8'bz;  // Driver driver_11
  assign driver_7_out = ctl_reg_in_hi ? db_hi_ds_in : 8'bz;  // Driver driver_12
  not not_3 (not_3_out, reg_gp_we);
endmodule
