// Digital circuit reg-latch-_est.dig as structural Verilog
module reg_latch__est (
  input  we,
  input  oe,
  input  [7:0] db_in,
  input  clk,
  output [7:0] db_out
);

  wire driver_1_out;
  wire [7:0] d_ff_1_q;

  assign driver_1_out = we ? clk : 1'bz;  // Driver driver_1
  D_FF #(.Bits(8)) d_ff_1 (.D(db_in), .C(driver_1_out), .Q(d_ff_1_q));  // open: nQ
  assign db_out = oe ? d_ff_1_q : 8'bz;  // Driver driver_2

  // Notes on the sheet:
  //   db_out: 8 bi Bidirectional data bus
  //   db_in: Bi-directional 8 bit Data bus
endmodule

/* Test case Register Test:
clk  oe  we  db_in  db_out
0    0    0   0x5a   z
c    0    0   0x5a   z
0    0    1   0x5a   z
c    0    1   0x5a   z
0    1    0   0x5a   0x5a
C    0    1   0xa5   z
0    1    0   0xa5   0xa5
*/
