// Digital circuit reg_control_test.dig as structural Verilog
module reg_control_test (
  input  ctl_reg_gp_we,
  input  [1:0] ctl_reg_gp_hilo,
  input  [1:0] ctl_reg_gp_sel,
  input  ctl_reg_ex_de_hl,
  input  nreset,
  input  ctl_reg_exx,
  input  use_ixiy,
  input  use_ix,
  input  ctl_reg_exx_af,
  input  ctl_reg_use_sp,
  input  ctl_reg_sys_we_hi,
  input  ctl_reg_sys_we,
  input  ctl_reg_sys_we_lo,
  input  [1:0] ctl_reg_sys_hilo,
  input  ctl_reg_sel_ir,
  input  ctl_sw_4d,
  input  ct_l_reg_not_pc,
  input  ctl_reg_sel_pc,
  input  ctl_reg_sel_wz,
  input  clk,
  output reg_gp_we,
  output reg_sel_gp_lo,
  output reg_sel_gp_hi,
  output reg_sel_bc2,
  output reg_sel_bc,
  output reg_sel_de2,
  output reg_sel_h2,
  output reg_sel_de,
  output reg_sel_hl,
  output reg_sel_ix,
  output reg_sel_iy,
  output reg_sel_sp,
  output reg_sys_we_hi,
  output reg_sys_we_lo,
  output reg_sel_sys_lo,
  output reg_sel_sys_hi,
  output reg_sw_4d_hi,
  output reg_sw_4d_lo,
  output reg_sel_ir,
  output reg_sel_pc,
  output reg_sel_wz,
  output reg_sel_af2,
  output reg_sel_af
);

  wire and_1_out, and_2_out, and_3_out, and_4_out, and_7_out, and_8_out, and_9_out, and_10_out, and_11_out,
       and_13_out, and_15_out, and_16_out, and_17_out, and_18_out, and_19_out, and_20_out, and_21_out,
       and_22_out, not_1_out, not_2_out, not_3_out, not_4_out, not_5_out, not_6_out, not_7_out, not_8_out,
       not_9_out, not_10_out, not_11_out, not_12_out, not_13_out, not_14_out, or_3_out, or_4_out, or_5_out,
       or_6_out, t_as_1_q, t_as_2_q, t_as_3_q, t_as_4_q;

  not not_1 (not_1_out, ctl_reg_gp_sel[0]);
  not not_2 (not_2_out, ctl_reg_gp_sel[1]);
  not not_3 (not_3_out, ctl_reg_gp_sel[1]);
  not not_4 (not_4_out, ctl_reg_gp_sel[0]);
  T_AS t_as_1 (.T(ctl_reg_exx), .Clk(clk), .Clr(nreset), .Q(t_as_1_q));  // open: Q_2
  and and_1 (and_1_out, not_4_out, ctl_reg_gp_sel[1]);
  and and_2 (and_2_out, not_1_out, not_2_out);
  and and_3 (and_3_out, ctl_reg_gp_sel[0], not_3_out);
  not not_5 (not_5_out, t_as_1_q);
  and and_4 (and_4_out, ctl_reg_gp_sel[0], ctl_reg_gp_sel[1]);
  not not_6 (not_6_out, use_ixiy);
  not not_7 (not_7_out, ctl_reg_use_sp);
  and and_5 (reg_sel_bc2, and_2_out, t_as_1_q);
  and and_6 (reg_sel_bc, and_2_out, not_5_out);
  and and_7 (and_7_out, ctl_reg_ex_de_hl, t_as_1_q);
  and and_8 (and_8_out, ctl_reg_ex_de_hl, not_5_out);
  and and_9 (and_9_out, and_1_out, not_6_out);
  and and_10 (and_10_out, and_1_out, use_ixiy);
  T_AS t_as_2 (.T(and_7_out), .Clk(clk), .Clr(nreset), .Q(t_as_2_q));  // open: Q_2
  T_AS t_as_3 (.T(and_8_out), .Clk(clk), .Clr(nreset), .Q(t_as_3_q));  // open: Q_2
  and and_11 (and_11_out, and_4_out, not_7_out);
  and and_12 (reg_sel_sp, and_4_out, ctl_reg_use_sp);
  or or_1 (reg_sys_we_hi, ctl_reg_sys_we_hi, ctl_reg_sys_we);
  or or_2 (reg_sys_we_lo, ctl_reg_sys_we, ctl_reg_sys_we_lo);
  not not_8 (not_8_out, ctl_reg_sys_hilo[0]);
  not not_9 (not_9_out, ct_l_reg_not_pc);
  not not_10 (not_10_out, t_as_2_q);
  not not_11 (not_11_out, t_as_3_q);
  T_AS t_as_4 (.T(ctl_reg_exx_af), .Clk(clk), .Clr(nreset), .Q(t_as_4_q));  // open: Q_2
  and and_13 (and_13_out, ctl_reg_sys_hilo[1], not_8_out, ctl_reg_sel_ir);
  and and_14 (reg_sel_pc, ctl_reg_sel_pc, not_9_out);
  not not_12 (not_12_out, and_13_out);
  and and_15 (and_15_out, t_as_2_q, and_9_out);
  and and_16 (and_16_out, not_10_out, and_3_out);
  and and_17 (and_17_out, not_10_out, and_9_out);
  and and_18 (and_18_out, t_as_2_q, and_3_out);
  and and_19 (and_19_out, t_as_3_q, and_9_out);
  and and_20 (and_20_out, not_11_out, and_3_out);
  and and_21 (and_21_out, not_11_out, and_9_out);
  and and_22 (and_22_out, t_as_3_q, and_3_out);
  and and_23 (reg_sw_4d_hi, ctl_sw_4d, not_12_out);
  or or_3 (or_3_out, and_15_out, and_16_out);
  or or_4 (or_4_out, and_17_out, and_18_out);
  or or_5 (or_5_out, and_19_out, and_20_out);
  or or_6 (or_6_out, and_21_out, and_22_out);
  not not_13 (not_13_out, use_ix);
  not not_14 (not_14_out, t_as_4_q);
  and and_24 (reg_sel_ix, and_10_out, use_ix);
  and and_25 (reg_sel_iy, and_10_out, not_13_out);
  and and_26 (reg_sel_af2, t_as_4_q, and_11_out);
  and and_27 (reg_sel_af, not_14_out, and_11_out);
  and and_28 (reg_sel_de2, t_as_1_q, or_3_out);
  and and_29 (reg_sel_h2, t_as_1_q, or_4_out);
  and and_30 (reg_sel_de, not_5_out, or_5_out);
  and and_31 (reg_sel_hl, not_5_out, or_6_out);

  assign reg_gp_we = ctl_reg_gp_we;
  assign reg_sel_gp_hi = ctl_reg_gp_hilo[1];
  assign reg_sel_gp_lo = ctl_reg_gp_hilo[0];
  assign reg_sel_ir = ctl_reg_sel_ir;
  assign reg_sel_sys_hi = ctl_reg_sys_hilo[1];
  assign reg_sel_sys_lo = ctl_reg_sys_hilo[0];
  assign reg_sel_wz = ctl_reg_sel_wz;
  assign reg_sw_4d_lo = ctl_sw_4d;

  // Other names for the same wires on the sheet: Reg_sys_we_lo_t = ctl_reg_sys_hilo[0]

  // Notes on the sheet:
  //   reg_sel_de2: reg-sel-de2
  //   ctl-reg-op-sel(1)
  //   ctl-reg-op-sel(0)
  //   Block PC (use for override WZ. HL for jumps)
  //   2'b00
  //   2'b01
  //   2'b10
  //   Use SP instead of AF
  //   2b'11
  //   BC
  //   DE
  //   bank-exx
  //   HL
  //   ctl-reg-sys-hilo(0)
  //   ctl-reg-sys-hilo(1)
  //   AF
  //   Use AF or SP
  //   Set 1
  //   Set 0
  //   bank-sel-de2
  //   bank-hi-de1
  //   de = AC+/AB
  //   hl = /AC+AB
  //   Fix bus contention when reading I reg and bypassing int # (used for interrupt handling)
  //   ctl-reg-gp-hilo[0]
  //   ctl-reg-gp-hilo[1]
  //   bank-af
endmodule
