// Digital circuit reg_latch.dig as structural Verilog
module reg_latch (
  input  oe,
  input  we,
  input  clk,
  output [7:0] db
);

  wire driver_1_out;
  wire [7:0] d_ff_1_q;

  assign driver_1_out = we ? clk : 1'bz;  // Driver driver_1
  D_FF #(.Bits(8)) d_ff_1 (.D(db), .C(driver_1_out), .Q(d_ff_1_q));  // open: nQ
  assign db = oe ? d_ff_1_q : 8'bz;  // Driver driver_2
endmodule
