// Digital circuit reg_control.dig as structural Verilog
module reg_control (
  input  ctl_rg_gp_we,
  input  [1:0] ctl_reg_gp_hilo,
  input  [1:0] ctl_reg_gp_sel,
  input  ctl_reg_ex_de_hl,
  output reg_gp_we,
  output reg_sel_gp_lo,
  output reg_sel_gp_hi,
  output reg_sel_bc2,
  output reg_sel_bc
);

  wire and_1_out, and_5_out, not_1_out, not_2_out, not_3_out, undriven, undriven_2;

  not not_1 (not_1_out, ctl_reg_gp_sel[0]);
  not not_2 (not_2_out, ctl_reg_gp_sel[1]);
  not not_3 (not_3_out, ctl_reg_gp_sel[1]);
  and and_1 (and_1_out, not_1_out, not_2_out);
  // And and_2 has open pins: In_1=ctl_reg_gp_sel[0], In_2=not_3_out, out=open
  and and_3 (reg_sel_bc2, and_1_out, undriven);
  and and_4 (reg_sel_bc, and_1_out, undriven_2);
  and and_5 (and_5_out, ctl_reg_ex_de_hl, undriven);
  T_FF t_ff_1 (.T(and_5_out));  // open: C, Q, nQ

  assign reg_gp_we = ctl_rg_gp_we;
  assign reg_sel_gp_hi = ctl_reg_gp_hilo[1];
  assign reg_sel_gp_lo = ctl_reg_gp_hilo[0];

  // Notes on the sheet:
  //   2'b00
  //   BC
  //   DE
  //   Set 1
  //   Set 0
  //   ctl-reg-gp-hilo[0]
  //   ctl-reg-gp-hilo[1]
endmodule
