// Digital circuit register_file.dig as structural Verilog
module register_file (
  input  [7:0] db_hi_as,
  input  clk,
  input  [7:0] db_lo_as,
  input  reg_sys_we_hi,
  input  reg_sel_sys_hi,
  input  reg_sel_sys_lo,
  input  reg_sel_gp_hi,
  input  [7:0] db_hi_ds,
  input  [7:0] db_lo_ds,
  input  reg_sys_we_lo,
  input  reg_gp_we,
  input  reg_sel_gp_lo,
  input  reg_sel_ir,
  input  reg_sel_pc,
  input  reg_sel_4d_hi,
  input  reg_sel_4d_lo,
  input  ctl_sw_4u,
  input  reg_sel_wz,
  input  reg_sel_sp,
  input  reg_sel_iy,
  input  reg_sel_ix,
  input  reg_sel_hl2,
  input  reg_sel_hl,
  input  reg_sel_de2,
  input  reg_sel_de,
  input  reg_sel_bc2,
  input  reg_sel_bc,
  input  reg_sel_af2,
  input  reg_sel_af,
  input  ctl_reg_in_hi,
  input  ctl_reg_in_lo,
  input  ctl_reg_out_hi,
  input  ctl_reg_out_lo
);

  wire and_1_out, and_3_out, and_5_out, and_6_out, and_9_out, and_10_out, and_13_out, and_15_out, and_17_out,
       and_18_out, and_21_out, and_23_out, and_25_out, and_26_out, and_29_out, and_31_out, and_33_out,
       and_34_out, and_37_out, and_39_out, and_41_out, and_42_out, and_45_out, and_47_out, and_49_out,
       and_50_out, and_53_out, and_55_out, not_1_out, not_2_out, not_3_out, reg_latch_1_p1, reg_latch_1_p4,
       reg_latch_3_p4, reg_latch_4_p4, reg_latch_5_p4, reg_latch_6_p4, reg_latch_7_p1, reg_latch_7_p4,
       reg_latch_9_p4, reg_latch_10_p4, reg_latch_11_p1, reg_latch_11_p4, reg_latch_13_p4, reg_latch_14_p4,
       reg_latch_15_p1, reg_latch_15_p4, reg_latch_17_p4, reg_latch_18_p4, reg_latch_19_p1, reg_latch_19_p4,
       reg_latch_21_p4, reg_latch_22_p4, reg_latch_23_p1, reg_latch_23_p4, reg_latch_25_p4, reg_latch_26_p4,
       reg_latch_27_p1, reg_latch_27_p4;
  wire [7:0] driver_1_out, driver_3_out;

  not not_1 (not_1_out, reg_sys_we_lo);
  not not_2 (not_2_out, reg_sys_we_hi);
  and and_1 (and_1_out, reg_sel_sys_lo, reg_sys_we_lo, reg_sel_ir);
  // reg_latch reg_latch_1: pin names not known; wires that end beside it: reg_latch_1_p1, db_hi_as, clk, reg_latch_1_p4
  and and_2 (reg_latch_1_p1, reg_sel_ir, reg_sel_sys_hi, not_2_out);
  and and_3 (and_3_out, not_1_out, reg_sel_sys_lo, reg_sel_ir);
  // reg_latch reg_latch_2: pin names not known; wires that end beside it: and_1_out, clk, db_lo_as, and_3_out
  and and_4 (reg_latch_1_p4, reg_sel_ir, reg_sys_we_hi, reg_sel_sys_hi);
  and and_5 (and_5_out, reg_sel_pc, reg_sel_sys_hi, not_2_out);
  and and_6 (and_6_out, reg_sel_sys_lo, reg_sys_we_lo, reg_sel_pc);
  // reg_latch reg_latch_3: pin names not known; wires that end beside it: and_6_out, clk, db_lo_as, reg_latch_3_p4
  // reg_latch reg_latch_4: pin names not known; wires that end beside it: and_5_out, db_hi_as, clk, reg_latch_4_p4
  and and_7 (reg_latch_4_p4, reg_sel_pc, reg_sys_we_hi, reg_sel_sys_hi);
  and and_8 (reg_latch_3_p4, not_1_out, reg_sel_sys_lo, reg_sel_pc);
  assign driver_1_out = ctl_sw_4u ? db_lo_as : 8'bz;  // Driver driver_1
  assign db_lo_as = reg_sel_4d_lo ? driver_1_out : 8'bz;  // Driver driver_2
  assign driver_3_out = ctl_sw_4u ? db_hi_as : 8'bz;  // Driver driver_3
  assign db_hi_as = reg_sel_4d_hi ? driver_3_out : 8'bz;  // Driver driver_4
  and and_9 (and_9_out, reg_sel_wz, reg_sel_sys_hi, not_2_out);
  and and_10 (and_10_out, reg_sel_sys_lo, reg_sys_we_lo, reg_sel_wz);
  // reg_latch reg_latch_5: pin names not known; wires that end beside it: and_10_out, clk, driver_1_out, reg_latch_5_p4
  // reg_latch reg_latch_6: pin names not known; wires that end beside it: and_9_out, driver_3_out, clk, reg_latch_6_p4
  and and_11 (reg_latch_6_p4, reg_sel_wz, reg_sys_we_hi, reg_sel_sys_hi);
  and and_12 (reg_latch_5_p4, not_1_out, reg_sel_sys_lo, reg_sel_wz);
  and and_13 (and_13_out, reg_sel_gp_lo, reg_gp_we, reg_sel_sp);
  // reg_latch reg_latch_7: pin names not known; wires that end beside it: reg_latch_7_p1, driver_3_out, clk, reg_latch_7_p4
  and and_14 (reg_latch_7_p1, reg_sel_sp, reg_sel_gp_hi, not_2_out);
  and and_15 (and_15_out, not_3_out, reg_sel_gp_lo, reg_sel_sp);
  // reg_latch reg_latch_8: pin names not known; wires that end beside it: and_13_out, clk, driver_1_out, and_15_out
  and and_16 (reg_latch_7_p4, reg_sel_sp, reg_sys_we_hi, reg_sel_gp_hi);
  and and_17 (and_17_out, reg_sel_iy, reg_sel_gp_hi, not_2_out);
  and and_18 (and_18_out, reg_sel_gp_lo, reg_gp_we, reg_sel_iy);
  // reg_latch reg_latch_9: pin names not known; wires that end beside it: and_18_out, clk, driver_1_out, reg_latch_9_p4
  // reg_latch reg_latch_10: pin names not known; wires that end beside it: and_17_out, driver_3_out, clk, reg_latch_10_p4
  and and_19 (reg_latch_10_p4, reg_sel_iy, reg_sys_we_hi, reg_sel_gp_hi);
  and and_20 (reg_latch_9_p4, not_3_out, reg_sel_gp_lo, reg_sel_iy);
  and and_21 (and_21_out, reg_sel_gp_lo, reg_gp_we, reg_sel_ix);
  // reg_latch reg_latch_11: pin names not known; wires that end beside it: reg_latch_11_p1, driver_3_out, clk, reg_latch_11_p4
  and and_22 (reg_latch_11_p1, reg_sel_ix, reg_sel_gp_hi, not_2_out);
  and and_23 (and_23_out, not_3_out, reg_sel_gp_lo, reg_sel_ix);
  // reg_latch reg_latch_12: pin names not known; wires that end beside it: and_21_out, clk, driver_1_out, and_23_out
  and and_24 (reg_latch_11_p4, reg_sel_ix, reg_sys_we_hi, reg_sel_gp_hi);
  and and_25 (and_25_out, reg_sel_hl2, reg_sel_gp_hi, not_2_out);
  and and_26 (and_26_out, reg_sel_gp_lo, reg_gp_we, reg_sel_hl2);
  // reg_latch reg_latch_13: pin names not known; wires that end beside it: and_26_out, clk, driver_1_out, reg_latch_13_p4
  // reg_latch reg_latch_14: pin names not known; wires that end beside it: and_25_out, driver_3_out, clk, reg_latch_14_p4
  and and_27 (reg_latch_14_p4, reg_sel_hl2, reg_sys_we_hi, reg_sel_gp_hi);
  and and_28 (reg_latch_13_p4, not_3_out, reg_sel_gp_lo, reg_sel_hl2);
  and and_29 (and_29_out, reg_sel_gp_lo, reg_gp_we, reg_sel_hl);
  // reg_latch reg_latch_15: pin names not known; wires that end beside it: reg_latch_15_p1, driver_3_out, clk, reg_latch_15_p4
  and and_30 (reg_latch_15_p1, reg_sel_hl, reg_sel_gp_hi, not_2_out);
  and and_31 (and_31_out, not_3_out, reg_sel_gp_lo, reg_sel_hl);
  // reg_latch reg_latch_16: pin names not known; wires that end beside it: and_29_out, clk, driver_1_out, and_31_out
  and and_32 (reg_latch_15_p4, reg_sel_hl, reg_sys_we_hi, reg_sel_gp_hi);
  and and_33 (and_33_out, reg_sel_de2, reg_sel_gp_hi, not_2_out);
  and and_34 (and_34_out, reg_sel_gp_lo, reg_gp_we, reg_sel_de2);
  // reg_latch reg_latch_17: pin names not known; wires that end beside it: and_34_out, clk, driver_1_out, reg_latch_17_p4
  // reg_latch reg_latch_18: pin names not known; wires that end beside it: and_33_out, driver_3_out, clk, reg_latch_18_p4
  and and_35 (reg_latch_18_p4, reg_sel_de2, reg_sys_we_hi, reg_sel_gp_hi);
  and and_36 (reg_latch_17_p4, not_3_out, reg_sel_gp_lo, reg_sel_de2);
  and and_37 (and_37_out, reg_sel_gp_lo, reg_gp_we, reg_sel_de);
  // reg_latch reg_latch_19: pin names not known; wires that end beside it: reg_latch_19_p1, driver_3_out, clk, reg_latch_19_p4
  and and_38 (reg_latch_19_p1, reg_sel_de, reg_sel_gp_hi, not_2_out);
  and and_39 (and_39_out, not_3_out, reg_sel_gp_lo, reg_sel_de);
  // reg_latch reg_latch_20: pin names not known; wires that end beside it: and_37_out, clk, driver_1_out, and_39_out
  and and_40 (reg_latch_19_p4, reg_sel_de, reg_sys_we_hi, reg_sel_gp_hi);
  and and_41 (and_41_out, reg_sel_bc2, reg_sel_gp_hi, not_2_out);
  and and_42 (and_42_out, reg_sel_gp_lo, reg_gp_we, reg_sel_bc2);
  // reg_latch reg_latch_21: pin names not known; wires that end beside it: and_42_out, clk, driver_1_out, reg_latch_21_p4
  // reg_latch reg_latch_22: pin names not known; wires that end beside it: and_41_out, driver_3_out, clk, reg_latch_22_p4
  and and_43 (reg_latch_22_p4, reg_sel_bc2, reg_sys_we_hi, reg_sel_gp_hi);
  and and_44 (reg_latch_21_p4, not_3_out, reg_sel_gp_lo, reg_sel_bc2);
  and and_45 (and_45_out, reg_sel_gp_lo, reg_gp_we, reg_sel_bc);
  // reg_latch reg_latch_23: pin names not known; wires that end beside it: reg_latch_23_p1, driver_3_out, clk, reg_latch_23_p4
  and and_46 (reg_latch_23_p1, reg_sel_bc, reg_sel_gp_hi, not_2_out);
  and and_47 (and_47_out, not_3_out, reg_sel_gp_lo, reg_sel_bc);
  // reg_latch reg_latch_24: pin names not known; wires that end beside it: and_45_out, clk, driver_1_out, and_47_out
  and and_48 (reg_latch_23_p4, reg_sel_bc, reg_sys_we_hi, reg_sel_gp_hi);
  and and_49 (and_49_out, reg_sel_af2, reg_sel_gp_hi, not_2_out);
  and and_50 (and_50_out, reg_sel_gp_lo, reg_gp_we, reg_sel_af2);
  // reg_latch reg_latch_25: pin names not known; wires that end beside it: and_50_out, clk, driver_1_out, reg_latch_25_p4
  // reg_latch reg_latch_26: pin names not known; wires that end beside it: and_49_out, driver_3_out, clk, reg_latch_26_p4
  and and_51 (reg_latch_26_p4, reg_sel_af2, reg_sys_we_hi, reg_sel_gp_hi);
  and and_52 (reg_latch_25_p4, not_3_out, reg_sel_gp_lo, reg_sel_af2);
  and and_53 (and_53_out, reg_sel_gp_lo, reg_gp_we, reg_sel_af);
  // reg_latch reg_latch_27: pin names not known; wires that end beside it: reg_latch_27_p1, driver_3_out, clk, reg_latch_27_p4
  and and_54 (reg_latch_27_p1, reg_sel_af, reg_sel_gp_hi, not_2_out);
  and and_55 (and_55_out, not_3_out, reg_sel_gp_lo, reg_sel_af);
  // reg_latch reg_latch_28: pin names not known; wires that end beside it: and_53_out, clk, driver_1_out, and_55_out
  and and_56 (reg_latch_27_p4, reg_sel_af, reg_sys_we_hi, reg_sel_gp_hi);
  assign db_lo_ds = ctl_reg_out_hi ? driver_1_out : 8'bz;  // Driver driver_5
  assign driver_1_out = ctl_reg_in_lo ? db_lo_ds : 8'bz;  // Driver driver_6
  assign db_hi_ds = ctl_reg_out_lo ? driver_3_out : 8'bz;  // Driver driver_7
  assign driver_3_out = ctl_reg_in_hi ? db_hi_ds : 8'bz;  // Driver driver_8
  not not_3 (not_3_out, reg_gp_we);
endmodule
